# Fritzing sketch bonsaiaio_sketch (saved by Fritzing 0.9.3b)
breadboards: 3

parts:
  U1 = NodeMCU V3.0
  YwRobot_Power_Supply1 = YwRobot Breadboard Power Supply [part_number=545043]
  LCD1 = LCD screen
  R1 = Rotary Potentiometer (Small) [maximum_resistance=100kΩ package=THT]
  DHT1 = DHT11 Humitidy and Temperature Sensor
  U2 = 74HC595 [package="DIP16 [THT]"]
  LED1 = LED - 3mm [color="Red (633nm)" package="3 mm [THT]"]
  R4 = Resistor [tolerance=±5% resistance=220 package=THT]
  Componente1 = FC-28 Soil Hygrometer Module
  Componente2 = FC-28 Soil Hygrometer Module - Probe
  R5 = Rotary Potentiometer (Small) [maximum_resistance=100kΩ package=THT]
  Q1 = NPN-Transistor [package="SOT-23 [SMD]"]
  R6 = Resistor [tolerance=±5% resistance=220 package=THT]

nets:
  N1: U1.D0, R4.Pin_1
  N2: U1.D1, DHT1.VDD
  GND: U1.GND, YwRobot_Power_Supply1.GND#13, U2.GND, U2.OE, LED1.cathode
  N3: U1.D5, R6.Pin_1
  N4: U1.D6, U2.DS
  N5: U1.D7, U2.ST_CP
  N6: U1.D8, U2.SH_CP
  VIN: U1.Vin, YwRobot_Power_Supply1.VCC#9, U2.MR, U2.VCC
  N7: U1.A0, Componente1.AO
  N8: YwRobot_Power_Supply1.VCC#5, LCD1.VDD, R1.leg1, DHT1.DATA, R5.leg1, Q1.1
  VSS: YwRobot_Power_Supply1.GND#11, LCD1.VSS, LCD1.R/W, LCD1.LED-, R1.leg2, Componente1.GND, R5.leg2
  N9: LCD1.V0, R5.wiper
  N10: LCD1.RS, U2.Q7
  N11: LCD1.E, U2.Q0
  N12: LCD1.DB4, U2.Q4
  N13: LCD1.DB5, U2.Q3
  N14: LCD1.DB6, U2.Q2
  N15: LCD1.DB7, U2.Q1
  N16: LCD1.LED+, R1.wiper
  N17: LED1.anode, R4.Pin_0
  N18: Componente1.VCC, Q1.2
  N19: Componente1.POS, Componente2.NEG
  N20: Componente1.NEG, Componente2.POS
  N21: Q1.0, R6.Pin_0

custom parts:
  NodeMCU V3.0: NodeMcu V3 Lua WIFI Development Board
  YwRobot Breadboard Power Supply: The YwRobot Breadboard Power Supply (MB-V2) has two power rails; they can be 5V or 3V3. Power to the module can be provided through the female USB socket or through the A10 (female) 2.1mm power jack.
  DHT11 Humitidy and Temperature Sensor: DHT11 Humidity and Temperature Sensor
  FC-28 Soil Hygrometer Module: The FC-28 is a soil hygrometer module that uses the Texas Instruments LM393 comparator chip to provide an analog measurement of soil humidity. The digital output is high when soil moisture is over a certain threshold, as determined by adjusting the potentiometer.
  FC-28 Soil Hygrometer Module - Probe: The FC-28 is a soil hygrometer module that uses the Texas Instruments LM393 comparator chip to provide an analog measurement of soil humidity.
